# Fritzing sketch fsrwithresistor (saved by Fritzing 0.9.3b)
breadboards: 1

parts:
  MCU2 = Raspberry Pi Zero
  J3 = Basic Force Sensing Resistor (FSR) [package=THT]
  J4 = Basic Force Sensing Resistor (FSR) [package=THT]
  Part2 = Adafruit ADS1115 16Bit I2C ADC [part_number="Adafruit #1085"]
  Part3 = Adafruit ADS1115 16Bit I2C ADC [part_number="Adafruit #1085"]

nets:
  VDD: MCU2.pin_2, MCU2.pin_4, J3.pin_1, J4.pin_1, Part2.VDD, Part3.ADDR, Part3.VDD
  N1: MCU2.pin_3, Part2.SDA
  N2: MCU2.pin_5, Part2.SCL
  GND: MCU2.pin_6, MCU2.pin_9, MCU2.pin_20, MCU2.pin_25, J3.pin_0, J4.pin_0, Part2.AIN0, Part2.GND, Part3.AIN0, Part3.GND
  N3: MCU2.pin_27, Part3.SDA
  N4: MCU2.pin_28, Part3.SCL

custom parts:
  Adafruit ADS1115 16Bit I2C ADC: For microcontrollers without an analog-to-digital converter or when you want a higher-precision ADC, the ADS1115 provides 16-bit precision at 860 samples/second over I2C. The chip can be configured as 4 single-ended input channels, or two differential channels. As a nice bonus, it even includes a programmable gain amplifier, up to x16, to help boost up smaller single/differential signals to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
