# Fritzing sketch potentiometerfsrs (saved by Fritzing 0.9.3b)
breadboards: 1

parts:
  MCU1 = Raspberry Pi Zero
  J1 = Basic Force Sensing Resistor (FSR) [package=THT]
  J2 = Basic Force Sensing Resistor (FSR) [package=THT]
  Part1 = Adafruit ADS1115 16Bit I2C ADC [part_number="Adafruit #1085"]
  U1 = POT [package=pot_alpha_rv16af-20]

nets:
  N1: MCU1.pin_2, MCU1.pin_4, J1.pin_1, J2.pin_1, Part1.VDD, U1.E
  N2: MCU1.pin_3, Part1.SDA
  N3: MCU1.pin_5, Part1.SCL
  N4: MCU1.pin_6, MCU1.pin_9, MCU1.pin_20, MCU1.pin_39, J1.pin_0, J2.pin_0, Part1.GND, U1.A
  N5: Part1.AIN1, Part1.AIN0, U1.S

custom parts:
  Adafruit ADS1115 16Bit I2C ADC: For microcontrollers without an analog-to-digital converter or when you want a higher-precision ADC, the ADS1115 provides 16-bit precision at 860 samples/second over I2C. The chip can be configured as 4 single-ended input channels, or two differential channels. As a nice bonus, it even includes a programmable gain amplifier, up to x16, to help boost up smaller single/differential signals to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
